# Fritzing sketch Vertebral (saved by Fritzing 0.9.3b)
breadboards: 1

parts:
  Componente1 = Arduino Uno (Rev3) - ICSP
  S1 = Round Pushbutton
  Componente2 = TE466 [part_number=TE466]
  R1 = Resistor [tolerance=±5% resistance=220 package="0603 [SMD]"]
  S2 = Round Pushbutton
  R2 = Resistor [tolerance=±5% resistance=220 package="0603 [SMD]"]
  M1 = DC Motor
  U1 = LIPO-2000mAh [package=lipo-2000]

nets:
  N1: Componente1.A0, Componente2.EN
  N2: Componente1.A1, Componente2.GND, Componente2.SRC_-_GND, Componente2.SRC_-_POS, Componente2.CS, U1.+, U1.-
  N3: Componente1.5V, S1.leg1, S2.leg0
  N4: Componente1.D8, Componente1.D9_PWM, Componente1.GND, R1.Pin_0, R2.Pin_1
  N5: Componente1.D3_PWM, Componente2.PWM
  N6: Componente1.D4, Componente2.INB
  N7: Componente1.D5_PWM, Componente2.INA
  N8: S1.leg0, R2.Pin_0
  N9: Componente2.OUTA, M1.pin_1
  N10: Componente2.OUTB, M1.pin_2
  N11: R1.Pin_1, S2.leg1

custom parts:
  TE466: Description: This is essentially a ramped up version of our Ardumoto motor driver shield. For this monster shield we've replaced the L298 H-bridge with a pair of VNH2SP30 full-bridge motor drivers. We've also beefed up the support circuitry so this board is capable of driving a pair of high-current motors! The VIN and motor out are pitched for our 5mm screw terminals (not included), making it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
