# Fritzing sketch esquemático (saved by Fritzing 0.9.3b)
breadboards: 1

parts:
  Driver = TE466 [part_number=TE466]
  S1 = Round Pushbutton
  S2 = Round Pushbutton
  R1 = Resistor [tolerance=±5% resistance=220 package="0603 [SMD]"]
  R2 = Resistor [tolerance=±5% resistance=220 package="0603 [SMD]"]
  part = Arduino Uno (Rev3)
  M1 = DC Motor

nets:
  N1: Driver.OUTA, M1.pin_1
  N2: Driver.OUTB, M1.pin_2
  GND: Driver.GND, Driver.SRC_-_POS, Driver.CS, part.GND
  5V: Driver.5V, S1.leg0, S2.leg0, part.5V
  N3: Driver.EN, part.A0
  N4: Driver.PWM, part.D3_PWM
  N5: Driver.INA, part.D5_PWM
  N6: Driver.INB, part.D4
  N7: S1.leg1, R1.Pin_0
  N8: S2.leg1, R2.Pin_0
  N9: R1.Pin_1, part.D9_PWM
  N10: R2.Pin_1, part.D8

custom parts:
  TE466: Description: This is essentially a ramped up version of our Ardumoto motor driver shield. For this monster shield we've replaced the L298 H-bridge with a pair of VNH2SP30 full-bridge motor drivers. We've also beefed up the support circuitry so this board is capable of driving a pair of high-current motors! The VIN and motor out are pitched for our 5mm screw terminals (not included), making it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
